# Fritzing sketch Esquema_Cableado (saved by Fritzing 0.9.3b)
breadboards: 1

parts:
  J1 = STM32 Nucleo boards
  Componente1 = Arduino Motor Shield
  HC-SR04_Sensor_1 = HC-SR04 Ultrasonic Distance Sensor
  Componente2 = Bluetooth HC-05 Macho
  J2 = Basic Servo
  M1 = DC Motor
  M2 = DC Motor

nets:
  VCC: J1.U5V, HC-SR04_Sensor_1.VCC, Componente2.VCC, J2.vcc
  5V: J1.5V, J1.VIN
  GND: J1.GND, HC-SR04_Sensor_1.GND, Componente2.GND, J2.gnd
  N1: J1.PA8, HC-SR04_Sensor_1.TRIG, HC-SR04_Sensor_1.ECHO
  N2: J1.PB7, Componente2.TXD
  N3: Componente1.OUT3, M1.pin_1
  N4: Componente1.OUT4, M1.pin_2
  N5: Componente1.OUT2, M2.pin_1
  N6: Componente1.OUT1, M2.pin_2
